// Logisim project controlUnitALU.circ as structural Verilog: 7 circuits, main circuit model de inbus
module model_de_inbus (
  input  semnal_de_control,
  input  alt_semnal_de_control,
  input  [7:0] inbus,
  output [7:0] out_4,
  output [7:0] out_5
);

  wire clock_1_out;
  wire [7:0] controlled_buffer_1_out, controlled_buffer_2_out;

  Clock clock_1 (.out(clock_1_out));
  Register register_1 (.D(controlled_buffer_1_out), .en(semnal_de_control), .Q(out_4), .clk(clock_1_out));  // open: clr
  assign controlled_buffer_1_out = semnal_de_control ? inbus : 8'bz;  // Controlled_Buffer controlled_buffer_1
  Register register_2 (
    .D(controlled_buffer_2_out), .en(alt_semnal_de_control), .Q(out_5), .clk(clock_1_out));  // open: clr
  assign controlled_buffer_2_out = alt_semnal_de_control ? inbus : 8'bz;  // Controlled_Buffer controlled_buffer_2
endmodule

module counter (
  input  in_1,
  input  in_2,
  input  in_3,
  output [1:0] out_4
);

  wire not_1_out;

  J_K_Flip_Flop j_k_ff_1 (.J(in_2), .clk(in_1), .K(in_2), .Q(out_4[0]), .reset(not_1_out));  // open: Qn, preset, en
  not not_1 (not_1_out, in_3);
  J_K_Flip_Flop #(.trigger("falling")) j_k_ff_2 (
    .J(in_2), .clk(out_4[0]), .K(in_2), .Q(out_4[1]), .reset(not_1_out));  // open: Qn, preset, en
endmodule

module Sequence_CNT (
  input  in_1,
  input  in_2,
  input  in_3,
  input  in_4,
  output out_5,
  output out_6,
  output out_7,
  output out_8
);

  wire and_1_out, and_2_out, s_r_ff_1_q;
  wire [1:0] counter_1_out_4;

  S_R_Flip_Flop s_r_ff_1 (.S(in_1), .clk(in_3), .R(in_2), .Q(s_r_ff_1_q));  // open: Qn, preset, reset, en
  counter counter_1 (.out_4(counter_1_out_4), .in_3(and_2_out), .in_1(and_1_out), .in_2(in_3));
  and and_1 (and_1_out, s_r_ff_1_q, in_3);
  and and_2 (and_2_out, in_4, s_r_ff_1_q);
  Decoder #(.select(2), .enable("false")) decoder_1 (
    .out0(out_5), .out1(out_6), .out2(out_7), .out3(out_8), .sel(counter_1_out_4));
endmodule

module Control_Unit_inmultire (
  input  Begin,
  input  [1:0] op,
  input  CLK,
  input  nRST,
  input  Q_0,
  input  Q__1,
  input  Count7,
  input  A_7,
  output c0,
  output c1,
  output c2,
  output EN_Adunare,
  output EN_Scadere,
  output c3,
  output c4,
  output c5,
  output c6,
  output c7,
  output out_19,
  output ci0,
  output ci1,
  output ci2,
  output ci3,
  output ci4,
  output ci5,
  output ci6,
  output ci7,
  output ci8
);

  wire and_1_out, and_2_out, and_3_out, and_4_out, Cycle_0_q, Cycle_1_8_q, Cycle_9_q, not_1_out, not_3_out,
       not_4_out, not_5_out, not_6_out, not_7_out, not_8_out, not_9_out, not_10_out, not_11_out, not_12_out,
       not_13_out, or_1_out, or_2_out, or_3_out, or_4_out, sequence_cnt_1_out_5, sequence_cnt_1_out_6,
       sequence_cnt_1_out_7, sequence_cnt_1_out_8, xor_1_out;

  S_R_Flip_Flop #(.trigger("high")) Cycle_0 (
    .S(Begin), .clk(CLK), .R(and_2_out), .Q(Cycle_0_q), .reset(or_1_out));  // open: Qn, preset, en
  S_R_Flip_Flop Cycle_1_8 (
    .S(and_2_out), .clk(CLK), .R(and_1_out), .Q(Cycle_1_8_q), .reset(not_5_out));  // open: Qn, preset, en
  S_R_Flip_Flop Cycle_9 (
    .S(and_1_out), .clk(CLK), .R(out_19), .Q(Cycle_9_q), .reset(not_5_out));  // open: Qn, preset, en
  not not_1 (not_1_out, not_4_out);
  not not_2 (out_19, not_1_out);
  or or_1 (or_1_out, not_5_out, or_2_out);
  not not_3 (not_3_out, not_7_out);
  not not_4 (not_4_out, not_3_out);
  not not_5 (not_5_out, nRST);
  or or_2 (or_2_out, Cycle_1_8_q, Cycle_9_q);
  and and_1 (and_1_out, Cycle_1_8_q, Count7, sequence_cnt_1_out_8);
  not not_6 (not_6_out, not_11_out);
  not not_7 (not_7_out, not_8_out);
  not not_8 (not_8_out, not_6_out);
  and and_2 (and_2_out, Cycle_0_q, sequence_cnt_1_out_8);
  not not_9 (not_9_out, not_10_out);
  not not_10 (not_10_out, not_13_out);
  not not_11 (not_11_out, not_9_out);
  Sequence_CNT sequence_cnt_1 (
    .in_1(Begin), .in_2(out_19), .in_3(CLK), .in_4(nRST), .out_5(sequence_cnt_1_out_5),
    .out_6(sequence_cnt_1_out_6), .out_7(sequence_cnt_1_out_7), .out_8(sequence_cnt_1_out_8));
  not not_12 (not_12_out, or_4_out);
  not not_13 (not_13_out, not_12_out);
  and and_3 (and_3_out, sequence_cnt_1_out_7, A_7);
  xor xor_1 (xor_1_out, Q_0, Q__1);
  and and_4 (and_4_out, op[1], op[0]);
  or or_3 (or_3_out, sequence_cnt_1_out_6, and_3_out);
  or or_4 (or_4_out, c7, ci8);
  and and_5 (c0, ~op[0], op[1], sequence_cnt_1_out_5, Cycle_0_q);  // AND_Gate
  and and_6 (c1, ~op[0], op[1], sequence_cnt_1_out_6, Cycle_0_q);  // AND_Gate
  and and_7 (c2, ~op[0], op[1], Cycle_1_8_q, xor_1_out, sequence_cnt_1_out_5);  // AND_Gate
  and and_8 (c3, ~op[0], op[1], c2, Q_0, ~Q__1);  // AND_Gate
  and and_9 (c4, ~Count7, sequence_cnt_1_out_6, Cycle_1_8_q, ~op[0], op[1]);  // AND_Gate
  and and_10 (c5, ~op[0], op[1], sequence_cnt_1_out_5, Cycle_9_q);  // AND_Gate
  and and_11 (c6, ~op[0], op[1], sequence_cnt_1_out_6, Cycle_9_q);  // AND_Gate
  and and_12 (c7, ~op[0], op[1], sequence_cnt_1_out_8, Cycle_9_q);  // AND_Gate
  and and_13 (ci0, and_4_out, sequence_cnt_1_out_5, Cycle_0_q);
  and and_14 (ci1, and_4_out, sequence_cnt_1_out_6, Cycle_0_q);
  and and_15 (ci2, and_4_out, sequence_cnt_1_out_7, Cycle_0_q);
  and and_16 (ci3, and_4_out, sequence_cnt_1_out_5, Cycle_1_8_q, ~Count7);  // AND_Gate
  and and_17 (ci4, and_4_out, or_3_out, Cycle_1_8_q);
  and and_18 (ci5, ci4, and_4_out, sequence_cnt_1_out_6, Cycle_1_8_q);
  and and_19 (ci6, and_4_out, sequence_cnt_1_out_5, Cycle_9_q, A_7);
  and and_20 (ci7, and_4_out, sequence_cnt_1_out_6, Cycle_9_q);
  and and_21 (ci8, and_4_out, sequence_cnt_1_out_7, Cycle_9_q);
  and and_22 (EN_Adunare, ~op[1], ~op[0]);  // AND_Gate
  and and_23 (EN_Scadere, op[0], ~op[1]);  // AND_Gate

  // Notes on the sheet:
  //   nr par de invertoare pt delay
  //   00-adunare
  //   01-scadere
  //   10-inmultire
  //   11-impartire
endmodule

module booth_radix_2 (
  input  [7:0] Q_inbus,
  input  [7:0] M_inbus,
  input  clock,
  input  c0,
  input  c1,
  input  c2,
  input  c3,
  input  c4,
  input  c5,
  input  c6,
  input  c7,
  output Q_0,
  output Q__1,
  output count7,
  output [7:0] A_outbus,
  output [7:0] Q_outbus
);

  wire A_out, or_1_out, or_2_out;
  wire [2:0] counter_1_q;
  wire [7:0] A_q7, controlled_buffer_1_out, controlled_buffer_3_out, controlled_buffer_5_out, M_q7,
       multiplexer_1_out, parallel_adder_1_out_4, xor_1_out;
  wire [7:1] Q_q6;

  assign controlled_buffer_1_out = c0 ? {8{1'b0}} : 8'bz;  // Controlled_Buffer controlled_buffer_1
  Multiplexer #(.select(2), .width(8), .enable("false")) multiplexer_1 (
    .in1(controlled_buffer_1_out), .in2(parallel_adder_1_out_4), .out(multiplexer_1_out), .sel({c2, c0}));  // open: in0, in3
  or or_1 (or_1_out, c0, c2);
  or or_2 (or_2_out, c4, c5);
  // Probe on parallel_adder_1_out_4
  Shift_Register A (
    .shift(or_2_out), .in(A_q7[7]), .clk(clock), .out(A_out), .load(or_1_out), .d0(multiplexer_1_out[7]),
    .q0(A_q7[7]), .d1(multiplexer_1_out[6]), .q1(A_q7[6]), .d2(multiplexer_1_out[5]), .q2(A_q7[5]),
    .d3(multiplexer_1_out[4]), .q3(A_q7[4]), .d4(multiplexer_1_out[3]), .q4(A_q7[3]),
    .d5(multiplexer_1_out[2]), .q5(A_q7[2]), .d6(multiplexer_1_out[1]), .q6(A_q7[1]),
    .d7(multiplexer_1_out[0]), .q7(A_q7[0]));  // open: clr
  assign A_outbus = c6 ? A_q7 : 8'bz;  // Controlled_Buffer controlled_buffer_2
  // Probe on A_q7
  assign controlled_buffer_3_out = c1 ? Q_inbus : 8'bz;  // Controlled_Buffer controlled_buffer_3
  Parallel_Adder parallel_adder_1 (
    .out_4(parallel_adder_1_out_4), .x_7_0(A_q7), .y_7_0(xor_1_out), .in_1(c3));  // open: Overflow, Cout
  Shift_Register #(.length(9)) Q (
    .shift(or_2_out), .in(A_out), .clk(clock), .load(c1), .d0(controlled_buffer_3_out[7]), .q0(Q_q6[7]),
    .d1(controlled_buffer_3_out[6]), .q1(Q_q6[6]), .d2(controlled_buffer_3_out[5]), .q2(Q_q6[5]),
    .d3(controlled_buffer_3_out[4]), .q3(Q_q6[4]), .d4(controlled_buffer_3_out[3]), .q4(Q_q6[3]),
    .d5(controlled_buffer_3_out[2]), .q5(Q_q6[2]), .d6(controlled_buffer_3_out[1]), .q6(Q_q6[1]),
    .d7(controlled_buffer_3_out[0]), .q7(Q_0), .d8(1'b0), .q8(Q__1));  // open: out, clr
  // Probe on xor_1_out
  assign Q_outbus = c7 ? {Q_q6, Q_0} : 8'bz;  // Controlled_Buffer controlled_buffer_4
  assign xor_1_out = M_q7 ^ {8{c3}};  // XOR_Gate xor_1, 8 bits wide
  // Probe on counter_1_q
  Counter #(.width(3), .max('h7)) counter_1 (
    .load(c0), .D(3'b000), .count(c4), .Q(counter_1_q), .clk(clock));  // open: carry, clr
  and and_1 (count7, counter_1_q[2], counter_1_q[1], counter_1_q[0]);
  assign controlled_buffer_5_out = c0 ? M_inbus : 8'bz;  // Controlled_Buffer controlled_buffer_5
  Shift_Register M (
    .shift(1'b0), .clk(clock), .load(c0), .d0(controlled_buffer_5_out[7]), .q0(M_q7[7]),
    .d1(controlled_buffer_5_out[6]), .q1(M_q7[6]), .d2(controlled_buffer_5_out[5]), .q2(M_q7[5]),
    .d3(controlled_buffer_5_out[4]), .q3(M_q7[4]), .d4(controlled_buffer_5_out[3]), .q4(M_q7[3]),
    .d5(controlled_buffer_5_out[2]), .q5(M_q7[2]), .d6(controlled_buffer_5_out[1]), .q6(M_q7[1]),
    .d7(controlled_buffer_5_out[0]), .q7(M_q7[0]));  // open: in, out, clr
  // Probe on c3

  // Notes on the sheet:
  //   01
  //   10
  //   c4
  //   c5
  //   c0
  //   shift
  //   A[7]=A[7]
  //   c2
  //   c1
  //   c3
  //   Q[0]Q[-1]
  //   c0
  //   c4
  //   EXOR wordgate
  //   COUNT7
  //   c0
  //   c3
endmodule

module ALU (
  input  [7:0] in_1,
  input  [7:0] in_2,
  input  [1:0] in_3,
  input  in_4,
  input  in_5,
  output [7:0] out_6,
  output [7:0] out_7,
  output out_8
);

  wire booth_radix_2_1_count7, booth_radix_2_1_q_0, booth_radix_2_1_q__1, clock_1_out,
       control_unit_inmultire_1_c0, control_unit_inmultire_1_c1, control_unit_inmultire_1_c2,
       control_unit_inmultire_1_c3, control_unit_inmultire_1_c4, control_unit_inmultire_1_c5,
       control_unit_inmultire_1_c6, control_unit_inmultire_1_c7;

  Clock clock_1 (.out(clock_1_out));
  Control_Unit_inmultire control_unit_inmultire_1 (
    .Begin(in_4), .nRST(in_5), .Q_0(booth_radix_2_1_q_0), .Q__1(booth_radix_2_1_q__1),
    .Count7(booth_radix_2_1_count7), .c0(control_unit_inmultire_1_c0), .c1(control_unit_inmultire_1_c1),
    .c2(control_unit_inmultire_1_c2), .c3(control_unit_inmultire_1_c3), .c4(control_unit_inmultire_1_c4),
    .c5(control_unit_inmultire_1_c5), .c6(control_unit_inmultire_1_c6), .CLK(clock_1_out), .out_19(out_8),
    .c7(control_unit_inmultire_1_c7), .op(in_3));  // open: ci0, ci1, ci2, ci3, ci4, ci6, ci5, ci7, ci8, A_7, EN_Adunare, EN_Scadere
  booth_radix_2 booth_radix_2_1 (
    .A_outbus(out_6), .clock(clock_1_out), .Q_0(booth_radix_2_1_q_0), .Q__1(booth_radix_2_1_q__1),
    .count7(booth_radix_2_1_count7), .c0(control_unit_inmultire_1_c0), .c1(control_unit_inmultire_1_c1),
    .c2(control_unit_inmultire_1_c2), .c3(control_unit_inmultire_1_c3), .c4(control_unit_inmultire_1_c4),
    .c5(control_unit_inmultire_1_c5), .c6(control_unit_inmultire_1_c6), .c7(control_unit_inmultire_1_c7),
    .Q_inbus(in_1), .M_inbus(in_2), .Q_outbus(out_7));
endmodule

module Restoring_Div (
  input  [7:0] in_1,
  input  c4,
  input  [1:0] in_3,
  input  in_4,
  input  in_5,
  output out_6,
  output [7:0] A,
  output [7:0] Q
);

  wire and_2_out, control_unit_inmultire_1_ci2, control_unit_inmultire_1_ci4, control_unit_inmultire_1_ci6,
       control_unit_inmultire_1_ci7, control_unit_inmultire_1_ci8, or_2_out, or_3_out, or_4_out, or_5_out,
       or_6_out, register_1_q;
  wire [0:0] shifter_1_out;
  wire [1:0] control_unit_inmultire_1_ci1;
  wire [1:1] controlled_buffer_5_out;
  wire [2:0] control_unit_inmultire_1_ci0;
  wire [3:0] counter_1_q;
  wire [6:0] not_1_out;
  wire [7:0] A_q, and_1_out, controlled_buffer_1_out, controlled_buffer_2_out, controlled_buffer_4_out,
       controlled_buffer_6_out, M_q, multiplexer_1_out, multiplexer_2_out, parallel_adder_1_out_4, Q_q,
       shifter_1_out_2, xor_1_out;
  wire [7:7] control_unit_inmultire_1_ci5, or_7_out;

  assign controlled_buffer_1_out = control_unit_inmultire_1_ci0[0] ? in_1 : 8'bz;  // Controlled_Buffer controlled_buffer_1
  or or_1 (control_unit_inmultire_1_ci0[2], control_unit_inmultire_1_ci6, control_unit_inmultire_1_ci4);
  Multiplexer #(.select(3), .width(8), .enable("false")) multiplexer_1 (
    .in1(controlled_buffer_1_out), .in2(shifter_1_out_2), .in4(parallel_adder_1_out_4),
    .out(multiplexer_1_out), .sel(control_unit_inmultire_1_ci0));  // open: in0, in3, in5, in6, in7
  or or_2 (or_2_out, control_unit_inmultire_1_ci0[0], or_3_out);
  or or_3 (or_3_out, control_unit_inmultire_1_ci0[1], control_unit_inmultire_1_ci4);
  // Probe on shifter_1_out_2
  assign controlled_buffer_2_out = control_unit_inmultire_1_ci0[1] ? A_q : 8'bz;  // Controlled_Buffer controlled_buffer_2
  Register u_A (.D(multiplexer_1_out), .en(or_2_out), .Q(A_q), .clk(c4));  // open: clr
  // Probe on parallel_adder_1_out_4
  assign A = control_unit_inmultire_1_ci7 ? parallel_adder_1_out_4 : 8'bz;  // Controlled_Buffer controlled_buffer_3
  assign controlled_buffer_4_out = control_unit_inmultire_1_ci1[0] ? in_1 : 8'bz;  // Controlled_Buffer controlled_buffer_4
  Shifter shifter_1 (.in(controlled_buffer_2_out), .\dist (3'b001), .out({shifter_1_out_2[7:1], shifter_1_out[0]}));
  // Probe on A_q
  // Probe on {shifter_1_out_2[0], not_1_out}
  not not_1 (not_1_out[0], parallel_adder_1_out_4[7]);
  Parallel_Adder parallel_adder_1 (
    .out_4(parallel_adder_1_out_4), .x_7_0(A_q), .y_7_0(and_1_out), .in_1(control_unit_inmultire_1_ci5[7]));  // open: Overflow, Cout
  Register #(.width(1)) register_1 (.D(parallel_adder_1_out_4[7]), .en(1'b1), .Q(register_1_q), .clk(c4));  // open: clr
  // Probe on {not_1_out[6:1], controlled_buffer_5_out[1], not_1_out[0]}
  Multiplexer #(.select(2), .width(8), .enable("false")) multiplexer_2 (
    .in0({not_1_out[6:1], controlled_buffer_5_out[1], not_1_out[0]}), .in1(controlled_buffer_4_out),
    .in2({shifter_1_out_2[0], not_1_out}), .out(multiplexer_2_out), .sel(control_unit_inmultire_1_ci1));  // open: in3
  Register u_Q (.D(multiplexer_2_out), .en(or_4_out), .Q(Q_q), .clk(c4));  // open: clr
  or or_4 (or_4_out, or_3_out, control_unit_inmultire_1_ci1[0]);
  assign and_1_out = xor_1_out & {8{or_7_out[7]}};  // AND_Gate and_1, 8 bits wide
  assign {shifter_1_out_2[0], not_1_out[6:1], controlled_buffer_5_out[1]} = or_5_out ? Q_q : 8'bz;  // Controlled_Buffer controlled_buffer_5
  or or_5 (or_5_out, control_unit_inmultire_1_ci0[1], or_6_out);
  or or_6 (or_6_out, control_unit_inmultire_1_ci8, control_unit_inmultire_1_ci1[1]);
  assign xor_1_out = M_q ^ {8{control_unit_inmultire_1_ci5[7]}};  // XOR_Gate xor_1, 8 bits wide
  // Probe on counter_1_q
  Counter #(.width(4), .max('hf)) counter_1 (
    .load(control_unit_inmultire_1_ci0[0]), .D(4'b0001), .count(control_unit_inmultire_1_ci0[1]),
    .Q(counter_1_q), .clk(c4));  // open: carry, clr
  and and_2 (and_2_out, counter_1_q[3], ~counter_1_q[2], ~counter_1_q[1], counter_1_q[0]);  // AND_Gate
  and and_3 (control_unit_inmultire_1_ci1[1], control_unit_inmultire_1_ci5[7], control_unit_inmultire_1_ci4);
  or or_7 (or_7_out[7], control_unit_inmultire_1_ci6, control_unit_inmultire_1_ci4);
  Control_Unit_inmultire control_unit_inmultire_1 (
    .Begin(in_4), .nRST(in_5), .Count7(and_2_out), .CLK(c4), .out_19(out_6), .op(in_3),
    .ci0(control_unit_inmultire_1_ci0[0]), .ci1(control_unit_inmultire_1_ci1[0]),
    .ci2(control_unit_inmultire_1_ci2), .ci3(control_unit_inmultire_1_ci0[1]),
    .ci4(control_unit_inmultire_1_ci4), .ci6(control_unit_inmultire_1_ci6),
    .ci5(control_unit_inmultire_1_ci5[7]), .ci7(control_unit_inmultire_1_ci7),
    .ci8(control_unit_inmultire_1_ci8), .A_7(register_1_q));  // open: Q_0, Q__1, c0, c1, c2, c3, c4, c5, c6, c7, EN_Adunare, EN_Scadere
  assign controlled_buffer_6_out = control_unit_inmultire_1_ci2 ? in_1 : 8'bz;  // Controlled_Buffer controlled_buffer_6
  Register M (.D(controlled_buffer_6_out), .en(control_unit_inmultire_1_ci2), .Q(M_q), .clk(c4));  // open: clr
  assign Q = control_unit_inmultire_1_ci8 ? {shifter_1_out_2[0], not_1_out[6:1], controlled_buffer_5_out[1]} : 8'bz;  // Controlled_Buffer controlled_buffer_7

  // Notes on the sheet:
  //   A
  //   c0
  //   c3
  //   Q
  //   c5
endmodule
